# Fritzing sketch Robot (saved by Fritzing 0.9.1b)
perfboards: 1

parts:
  Part1 = HC-SR04 Ultrasonic Rangemeter  # not connected
  M1 = DC Motor
  M2 = DC Motor
  LM35_TempSensor1 = LM35 TempSensor  # not connected
  LCD1 = LCD screen
  VCC1 = 4 x AAA Battery Mount
  Part2 = Arduino Uno (Rev3)
  Part3 = 2A MOTOR SHIELD 9
  U1 = SWITCH_SPDT [package=kps-1290]
  R1 = Resistor [tolerance=±5% resistance=1k package=THT]  # not connected
  R2 = Resistor [tolerance=±5% resistance=2k package=THT]  # not connected
  Part6 = Bluetooth HC-05 Macho  # not connected
  JP1 = Header 1 [package=1x01_offset]  # not connected
  JP2 = Header 1 [package=1x01_offset]  # not connected
  JP3 = Header 1 [package=1x01_offset]  # not connected
  JP4 = Header 1 [package=1x01_offset]  # not connected
  RE1 = Rotary Encoder [package=THT]  # not connected
  RE2 = Rotary Encoder [package=THT]  # not connected

nets:
  N1: M1.pin_1, Part3.M1+
  N2: M1.pin_2, Part3.M1-
  N3: M2.pin_1, Part3.M2+
  N4: M2.pin_2, Part3.M2-
  VSS: LCD1.VSS, LCD1.VDD, LCD1.V0
  N5: LCD1.RS, LCD1.R/W, LCD1.E
  N6: LCD1.DB4, LCD1.DB5, LCD1.DB6
  N7: LCD1.DB7, LCD1.LED+, LCD1.LED-
  N8: VCC1.-, Part3.GND#0
  N9: VCC1.+, U1.O
  N10: Part2.A0, Part3.A0
  N11: Part2.A1, Part3.A1
  N12: Part2.A2, Part3.A2
  N13: Part2.A3, Part3.A3
  N14: Part2.A4/SDA, Part3.A4
  N15: Part2.A5/SCL, Part3.A5
  N16: Part2.D8, Part3.D8
  N17: Part2.D9_PWM, Part3.D9
  N18: Part2.D10_PWM/SS, Part3.D10
  N19: Part2.D11_PWM/MOSI, Part3.D11
  N20: Part2.D12/MISO, Part3.D12
  N21: Part2.D13/SCK, Part3.D13
  N22: Part2.GND, Part3.GND#connector1pad-0-1-1-48-61, Part3.GND#connector1pad-0-1-9-9-4-9, Part3.GND#connector1pad-4-5-0-39-8-14
  N23: Part2.AREF, Part3.AFER
  N24: Part2.D1/TX, Part3.D1
  N25: Part2.D2, Part3.D2
  N26: Part2.D3_PWM, Part3.D3
  N27: Part2.D4, Part3.D4
  N28: Part2.D5_PWM, Part3.D5
  N29: Part2.D6_PWM, Part3.D6
  N30: Part2.D7, Part3.D7
  N31: Part2.RESET, Part3.RST
  3V3: Part2.3V3, Part3.3V3
  5V: Part2.5V, Part3.5V
  VIN: Part2.VIN, Part3.VIN
  N32: Part3.D0, U1.P
